// Logisim project ADD_02.circ as structural Verilog: 3 circuits, main circuit main
module main (
  input  [3:0] A,
  input  [3:0] B,
  output Overflow,
  output [3:0] S
);

  ADD_04 add_04_1 (.out_3(Overflow), .A(A), .B(B), .Soma(S));
endmodule

module ADD_01 (
  input  A,
  input  B,
  input  C,
  output S,
  output Vai_1
);

  wire and_1_out, and_2_out, or_1_out, xor_1_out;

  xor xor_1 (xor_1_out, C, B);
  or or_1 (or_1_out, C, B);
  xor xor_2 (S, xor_1_out, A);
  and and_1 (and_1_out, or_1_out, A);
  and and_2 (and_2_out, C, B);
  or or_2 (Vai_1, and_1_out, and_2_out);
endmodule

module ADD_04 (
  input  [3:0] B,
  input  [3:0] A,
  output out_3,
  output [3:0] Soma
);

  wire add_01_2_vai_1, add_01_3_vai_1, add_01_4_vai_1;

  ADD_01 add_01_1 (.S(Soma[3]), .Vai_1(out_3), .A(A[3]), .B(B[3]), .C(add_01_2_vai_1));
  ADD_01 add_01_2 (.S(Soma[2]), .Vai_1(add_01_2_vai_1), .A(A[2]), .B(B[2]), .C(add_01_3_vai_1));
  ADD_01 add_01_3 (.S(Soma[1]), .Vai_1(add_01_3_vai_1), .A(A[1]), .B(B[1]), .C(add_01_4_vai_1));
  ADD_01 add_01_4 (.S(Soma[0]), .Vai_1(add_01_4_vai_1), .A(A[0]), .B(B[0]), .C(1'b0));
endmodule
