// Logisim project Rot_Dir.circ as structural Verilog: 7 circuits, main circuit main
module main (
  input  [3:0] B,
  input  [3:0] A,
  input  [1:0] x_y,
  output [3:0] S,
  output [3:0] S_2,
  output Overflow,
  output Overflow_2,
  output [3:0] S_3,
  output [3:0] S_4
);

  ADD_04 add_04_1 (.A(A), .out_3(Overflow_2), .B(B), .Soma(S_3));
  // Probe on S_3
  SUB_04 sub_04_1 (.out_3(Overflow), .A(A), .B(B), .S(S_4));
  // Probe on S_4
  Rot_Dir rot_dir_1 (.a_b_c_d(A), .x_y(x_y), .A_B_C_D_2(S));
  Rot_Esq rot_esq_1 (.a_b_c_d(A), .x_y(x_y), .A_B_C_D_2(S_2));
endmodule

module ADD_01 (
  input  A,
  input  B,
  input  C,
  output S,
  output Vai_1
);

  wire and_1_out, and_2_out, or_1_out, xor_1_out;

  xor xor_1 (xor_1_out, C, B);
  or or_1 (or_1_out, C, B);
  xor xor_2 (S, xor_1_out, A);
  and and_1 (and_1_out, or_1_out, A);
  and and_2 (and_2_out, C, B);
  or or_2 (Vai_1, and_1_out, and_2_out);
endmodule

module SUB_04 (
  input  [3:0] B,
  input  [3:0] A,
  output out_3,
  output [3:0] S
);

  wire sub_01_2_vai_1, sub_01_3_vai_1, sub_01_4_vai_1;

  SUB_01 sub_01_1 (.VAI_1(out_3), .S(S[3]), .A(A[3]), .B(B[3]), .VEM_1(sub_01_2_vai_1));
  SUB_01 sub_01_2 (.VAI_1(sub_01_2_vai_1), .S(S[2]), .A(A[2]), .B(B[2]), .VEM_1(sub_01_3_vai_1));
  SUB_01 sub_01_3 (.VAI_1(sub_01_3_vai_1), .S(S[1]), .A(A[1]), .B(B[1]), .VEM_1(sub_01_4_vai_1));
  SUB_01 sub_01_4 (.VAI_1(sub_01_4_vai_1), .S(S[0]), .A(A[0]), .B(B[0]), .VEM_1(1'b0));
endmodule

module SUB_01 (
  input  A,
  input  B,
  input  VEM_1,
  output S,
  output VAI_1
);

  wire and_1_out, and_2_out, or_1_out, xor_1_out;

  xor xor_1 (xor_1_out, A, B);
  or or_1 (or_1_out, B, VEM_1);
  and and_1 (and_1_out, or_1_out, ~A);  // AND_Gate
  and and_2 (and_2_out, VEM_1, B);
  xor xor_2 (S, xor_1_out, VEM_1);
  or or_2 (VAI_1, and_1_out, and_2_out);
endmodule

module ADD_04 (
  input  [3:0] B,
  input  [3:0] A,
  output out_3,
  output [3:0] Soma
);

  wire add_01_2_vai_1, add_01_3_vai_1, add_01_4_vai_1;

  ADD_01 add_01_1 (.S(Soma[3]), .Vai_1(out_3), .A(A[3]), .B(B[3]), .C(add_01_2_vai_1));
  ADD_01 add_01_2 (.S(Soma[2]), .Vai_1(add_01_2_vai_1), .A(A[2]), .B(B[2]), .C(add_01_4_vai_1));
  ADD_01 add_01_3 (.S(Soma[0]), .Vai_1(add_01_3_vai_1), .A(A[0]), .B(B[0]), .C(1'b0));
  ADD_01 add_01_4 (.S(Soma[1]), .Vai_1(add_01_4_vai_1), .A(A[1]), .B(B[1]), .C(add_01_3_vai_1));
endmodule

module Rot_Esq (
  input  [3:0] a_b_c_d,
  input  [1:0] x_y,
  output [3:0] A_B_C_D_2
);

  wire and_1_out, and_2_out, and_3_out, and_4_out, and_5_out, and_6_out, and_7_out, and_8_out, and_9_out;

  and and_1 (and_1_out, ~x_y[1], ~x_y[0], a_b_c_d[3]);  // AND_Gate
  and and_2 (and_2_out, ~x_y[1], x_y[0], a_b_c_d[2]);  // AND_Gate
  and and_3 (and_3_out, x_y[1], ~x_y[0], a_b_c_d[0]);  // AND_Gate
  and and_4 (and_4_out, x_y[1], x_y[0], a_b_c_d[0]);
  and and_5 (and_5_out, ~x_y[1], ~x_y[0], a_b_c_d[2]);  // AND_Gate
  and and_6 (and_6_out, ~x_y[1], x_y[0], a_b_c_d[1]);  // AND_Gate
  and and_7 (and_7_out, x_y[1], ~x_y[0], a_b_c_d[0]);  // AND_Gate
  and and_8 (and_8_out, ~x_y[1], ~x_y[0], a_b_c_d[1]);  // AND_Gate
  and and_9 (and_9_out, ~x_y[1], x_y[0], a_b_c_d[0]);  // AND_Gate
  and and_10 (A_B_C_D_2[0], ~x_y[1], ~x_y[0], a_b_c_d[0]);  // AND_Gate
  or or_1 (A_B_C_D_2[3], and_1_out, and_2_out, and_3_out, and_4_out);
  or or_2 (A_B_C_D_2[2], and_5_out, and_6_out, and_7_out);
  or or_3 (A_B_C_D_2[1], and_8_out, and_9_out);
endmodule

module Rot_Dir (
  input  [3:0] a_b_c_d,
  input  [1:0] x_y,
  output [3:0] A_B_C_D_2
);

  wire and_1_out, and_2_out, and_3_out, and_4_out, and_5_out, and_6_out, and_7_out, and_8_out, and_9_out;

  and and_1 (and_1_out, ~x_y[1], ~x_y[0], a_b_c_d[0]);  // AND_Gate
  and and_2 (and_2_out, ~x_y[1], x_y[0], a_b_c_d[1]);  // AND_Gate
  and and_3 (and_3_out, x_y[1], ~x_y[0], a_b_c_d[3]);  // AND_Gate
  and and_4 (and_4_out, x_y[1], x_y[0], a_b_c_d[3]);
  and and_5 (and_5_out, ~x_y[1], ~x_y[0], a_b_c_d[1]);  // AND_Gate
  and and_6 (and_6_out, ~x_y[1], x_y[0], a_b_c_d[2]);  // AND_Gate
  and and_7 (and_7_out, x_y[1], ~x_y[0], a_b_c_d[3]);  // AND_Gate
  and and_8 (and_8_out, ~x_y[1], ~x_y[0], a_b_c_d[2]);  // AND_Gate
  and and_9 (and_9_out, ~x_y[1], x_y[0], a_b_c_d[3]);  // AND_Gate
  and and_10 (A_B_C_D_2[3], ~x_y[1], ~x_y[0], a_b_c_d[3]);  // AND_Gate
  or or_1 (A_B_C_D_2[0], and_1_out, and_2_out, and_3_out, and_4_out);
  or or_2 (A_B_C_D_2[1], and_5_out, and_6_out, and_7_out);
  or or_3 (A_B_C_D_2[2], and_8_out, and_9_out);
endmodule
