// Logisim project ULA.circ as structural Verilog: 12 circuits, main circuit main
module main (
  input  [3:0] B,
  input  [3:0] A,
  input  [1:0] x_y,
  output [3:0] S,
  output [3:0] S_2,
  output Overflow,
  output Overflow_2,
  output [3:0] S_3,
  output [3:0] S_4
);

  ADD_04 add_04_1 (.A(A), .out_3(Overflow_2), .B(B), .Soma(S_3));
  // Probe on S_3
  SUB_04 sub_04_1 (.out_3(Overflow), .A(A), .B(B), .S(S_4));
  // Probe on S_4
  Rot_Dir rot_dir_1 (.a_b_c_d(A), .x_y(x_y), .A_B_C_D_2(S));
  Rot_Esq rot_esq_1 (.a_b_c_d(A), .x_y(x_y), .A_B_C_D_2(S_2));
endmodule

module ADD_01 (
  input  A,
  input  B,
  input  C,
  output S,
  output Vai_1
);

  wire and_1_out, and_2_out, or_1_out, xor_1_out;

  xor xor_1 (xor_1_out, C, B);
  or or_1 (or_1_out, C, B);
  xor xor_2 (S, xor_1_out, A);
  and and_1 (and_1_out, or_1_out, A);
  and and_2 (and_2_out, C, B);
  or or_2 (Vai_1, and_1_out, and_2_out);
endmodule

module SUB_04 (
  input  [3:0] B,
  input  [3:0] A,
  output out_3,
  output [3:0] S
);

  wire sub_01_2_vai_1, sub_01_3_vai_1, sub_01_4_vai_1;

  SUB_01 sub_01_1 (.VAI_1(out_3), .S(S[3]), .A(A[3]), .B(B[3]), .VEM_1(sub_01_2_vai_1));
  SUB_01 sub_01_2 (.VAI_1(sub_01_2_vai_1), .S(S[2]), .A(A[2]), .B(B[2]), .VEM_1(sub_01_3_vai_1));
  SUB_01 sub_01_3 (.VAI_1(sub_01_3_vai_1), .S(S[1]), .A(A[1]), .B(B[1]), .VEM_1(sub_01_4_vai_1));
  SUB_01 sub_01_4 (.VAI_1(sub_01_4_vai_1), .S(S[0]), .A(A[0]), .B(B[0]), .VEM_1(1'b0));
endmodule

module SUB_01 (
  input  A,
  input  B,
  input  VEM_1,
  output S,
  output VAI_1
);

  wire and_1_out, and_2_out, or_1_out, xor_1_out;

  xor xor_1 (xor_1_out, A, B);
  or or_1 (or_1_out, B, VEM_1);
  and and_1 (and_1_out, or_1_out, ~A);  // AND_Gate
  and and_2 (and_2_out, VEM_1, B);
  xor xor_2 (S, xor_1_out, VEM_1);
  or or_2 (VAI_1, and_1_out, and_2_out);
endmodule

module ADD_04 (
  input  [3:0] B,
  input  [3:0] A,
  output out_3,
  output [3:0] Soma
);

  wire add_01_2_vai_1, add_01_3_vai_1, add_01_4_vai_1;

  ADD_01 add_01_1 (.S(Soma[3]), .Vai_1(out_3), .A(A[3]), .B(B[3]), .C(add_01_2_vai_1));
  ADD_01 add_01_2 (.S(Soma[2]), .Vai_1(add_01_2_vai_1), .A(A[2]), .B(B[2]), .C(add_01_4_vai_1));
  ADD_01 add_01_3 (.S(Soma[0]), .Vai_1(add_01_3_vai_1), .A(A[0]), .B(B[0]), .C(1'b0));
  ADD_01 add_01_4 (.S(Soma[1]), .Vai_1(add_01_4_vai_1), .A(A[1]), .B(B[1]), .C(add_01_3_vai_1));
endmodule

module Rot_Esq (
  input  [3:0] a_b_c_d,
  input  [1:0] x_y,
  output [3:0] A_B_C_D_2
);

  wire and_1_out, and_2_out, and_3_out, and_4_out, and_5_out, and_6_out, and_7_out, and_8_out, and_9_out;

  and and_1 (and_1_out, ~x_y[1], ~x_y[0], a_b_c_d[3]);  // AND_Gate
  and and_2 (and_2_out, ~x_y[1], x_y[0], a_b_c_d[2]);  // AND_Gate
  and and_3 (and_3_out, x_y[1], ~x_y[0], a_b_c_d[0]);  // AND_Gate
  and and_4 (and_4_out, x_y[1], x_y[0], a_b_c_d[0]);
  and and_5 (and_5_out, ~x_y[1], ~x_y[0], a_b_c_d[2]);  // AND_Gate
  and and_6 (and_6_out, ~x_y[1], x_y[0], a_b_c_d[1]);  // AND_Gate
  and and_7 (and_7_out, x_y[1], ~x_y[0], a_b_c_d[0]);  // AND_Gate
  and and_8 (and_8_out, ~x_y[1], ~x_y[0], a_b_c_d[1]);  // AND_Gate
  and and_9 (and_9_out, ~x_y[1], x_y[0], a_b_c_d[0]);  // AND_Gate
  and and_10 (A_B_C_D_2[0], ~x_y[1], ~x_y[0], a_b_c_d[0]);  // AND_Gate
  or or_1 (A_B_C_D_2[3], and_1_out, and_2_out, and_3_out, and_4_out);
  or or_2 (A_B_C_D_2[2], and_5_out, and_6_out, and_7_out);
  or or_3 (A_B_C_D_2[1], and_8_out, and_9_out);
endmodule

module Rot_Dir (
  input  [3:0] a_b_c_d,
  input  [1:0] x_y,
  output [3:0] A_B_C_D_2
);

  wire and_1_out, and_2_out, and_3_out, and_4_out, and_5_out, and_6_out, and_7_out, and_8_out, and_9_out;

  and and_1 (and_1_out, ~x_y[1], ~x_y[0], a_b_c_d[0]);  // AND_Gate
  and and_2 (and_2_out, ~x_y[1], x_y[0], a_b_c_d[1]);  // AND_Gate
  and and_3 (and_3_out, x_y[1], ~x_y[0], a_b_c_d[3]);  // AND_Gate
  and and_4 (and_4_out, x_y[1], x_y[0], a_b_c_d[3]);
  and and_5 (and_5_out, ~x_y[1], ~x_y[0], a_b_c_d[1]);  // AND_Gate
  and and_6 (and_6_out, ~x_y[1], x_y[0], a_b_c_d[2]);  // AND_Gate
  and and_7 (and_7_out, x_y[1], ~x_y[0], a_b_c_d[3]);  // AND_Gate
  and and_8 (and_8_out, ~x_y[1], ~x_y[0], a_b_c_d[2]);  // AND_Gate
  and and_9 (and_9_out, ~x_y[1], x_y[0], a_b_c_d[3]);  // AND_Gate
  and and_10 (A_B_C_D_2[3], ~x_y[1], ~x_y[0], a_b_c_d[3]);  // AND_Gate
  or or_1 (A_B_C_D_2[0], and_1_out, and_2_out, and_3_out, and_4_out);
  or or_2 (A_B_C_D_2[1], and_5_out, and_6_out, and_7_out);
  or or_3 (A_B_C_D_2[2], and_8_out, and_9_out);
endmodule

module DECODIFI (
  input  [2:0] in_1,
  output S0,
  output S1,
  output S2,
  output S3,
  output S4,
  output S5,
  output S6,
  output S7
);

  wire not_1_out, not_2_out, not_3_out, not_4_out, not_5_out, not_6_out, not_7_out, not_8_out, not_9_out,
       not_10_out, not_11_out, not_12_out;

  and and_1 (S7, in_1[2], in_1[1], in_1[0]);
  not not_1 (not_1_out, in_1[2]);
  not not_2 (not_2_out, in_1[1]);
  not not_3 (not_3_out, in_1[0]);
  not not_4 (not_4_out, in_1[2]);
  not not_5 (not_5_out, in_1[1]);
  not not_6 (not_6_out, in_1[2]);
  not not_7 (not_7_out, in_1[0]);
  not not_8 (not_8_out, in_1[2]);
  not not_9 (not_9_out, in_1[1]);
  not not_10 (not_10_out, in_1[0]);
  not not_11 (not_11_out, in_1[1]);
  not not_12 (not_12_out, in_1[0]);
  and and_2 (S0, not_1_out, not_2_out, not_3_out);
  and and_3 (S1, not_4_out, not_5_out, in_1[0]);
  and and_4 (S2, not_6_out, in_1[1], not_7_out);
  and and_5 (S3, not_8_out, in_1[1], in_1[0]);
  and and_6 (S4, in_1[2], not_9_out, not_10_out);
  and and_7 (S5, in_1[2], not_11_out, in_1[0]);
  and and_8 (S6, in_1[2], in_1[1], not_12_out);
endmodule

// S
module Buffer_4 (
  input  [3:0] E,
  input  C,
  output [3:0] S
);

  assign S[3] = C ? E[3] : 1'bz;  // Controlled_Buffer controlled_buffer_1
  assign S[2] = C ? E[2] : 1'bz;  // Controlled_Buffer controlled_buffer_2
  assign S[1] = C ? E[1] : 1'bz;  // Controlled_Buffer controlled_buffer_3
  assign C = C ? E[0] : 1'bz;  // Controlled_Buffer controlled_buffer_4

  assign S[0] = C;
endmodule

module OR_4 (
  input  [3:0] B,
  input  [3:0] A,
  output [3:0] Soma
);

  or or_1 (Soma[3], A[3], B[3]);
  or or_2 (Soma[2], A[2], B[2]);
  or or_3 (Soma[1], A[1], B[1]);
  or or_4 (Soma[0], A[0], B[0]);
endmodule

module NOT_4 (
  input  [3:0] E,
  output [3:0] S
);

  not not_1 (S[3], E[3]);
  not not_2 (S[2], E[2]);
  not not_3 (S[1], E[1]);
  not not_4 (S[0], E[0]);
endmodule

module ULA (
  input  in_1,
  input  [3:0] B,
  input  [3:0] A,
  output Overflow,
  output [3:0] S,
  output Zero
);

  wire add_04_1_out_3, and_1_out, and_2_out, buffer_1_out, decodifi_1_s0, decodifi_1_s1, decodifi_1_s2,
       decodifi_1_s3, decodifi_1_s4, decodifi_1_s5, decodifi_1_s6, decodifi_1_s7, sub_04_1_out_3;
  wire [3:0] add_04_1_soma, buffer_4_7_s, not_4_1_s, or_4_1_soma, rot_esq_1_a_b_c_d_2, sub_04_1_s;

  or or_1 (Overflow, and_1_out, and_2_out);
  and and_1 (and_1_out, add_04_1_out_3, decodifi_1_s1);
  and and_2 (and_2_out, sub_04_1_out_3, decodifi_1_s2);
  DECODIFI decodifi_1 (
    .S0(decodifi_1_s0), .S1(decodifi_1_s1), .S2(decodifi_1_s2), .S3(decodifi_1_s3), .S4(decodifi_1_s4),
    .S5(decodifi_1_s5), .S6(decodifi_1_s6), .S7(decodifi_1_s7));  // open: in_1
  Buffer_4 buffer_4_1 (.E(B), .S(S), .C(decodifi_1_s0));
  ADD_04 add_04_1 (.A(A), .out_3(add_04_1_out_3), .B(B), .Soma(add_04_1_soma));
  Buffer_4 buffer_4_2 (.E(add_04_1_soma), .S(S), .C(decodifi_1_s1));
  Buffer_4 buffer_4_3 (.E(sub_04_1_s), .S(S), .C(decodifi_1_s2));
  OR_4 or_4_1 (.A(A), .B(B), .Soma(or_4_1_soma));
  SUB_04 sub_04_1 (.out_3(sub_04_1_out_3), .A(A), .B(B), .S(sub_04_1_s));
  Buffer_4 buffer_4_4 (.E(or_4_1_soma), .S(S), .C(decodifi_1_s3));
  Buffer_4 buffer_4_5 (.E(not_4_1_s), .S(S), .C(decodifi_1_s4));
  nor nor_1 (Zero, S[0], S[1], S[2], S[3], decodifi_1_s6, decodifi_1_s7);
  NOT_4 not_4_1 (.E(B), .S(not_4_1_s));
  Rot_Esq rot_esq_1 (.a_b_c_d(A), .x_y(B[1:0]), .A_B_C_D_2(rot_esq_1_a_b_c_d_2));
  Rot_Dir rot_dir_1 (.a_b_c_d(A), .x_y(B[1:0]), .A_B_C_D_2(A));
  Buffer_4 buffer_4_6 (.E(buffer_4_7_s), .S(S), .C(decodifi_1_s5));
  Buffer_4 buffer_4_7 (.E(rot_esq_1_a_b_c_d_2), .S(buffer_4_7_s), .C(buffer_1_out));
  buf buffer_1 (buffer_1_out, in_1);
  Buffer_4 buffer_4_8 (.E(A), .S(buffer_4_7_s), .C(in_1));
endmodule
